# Fritzing sketch client-03 (saved by Fritzing 0.9.3b)
circuit board: 3.75729cm x 2.15354cm

parts:
  J1 = female pin header, 2 pins [form="♀ (female)"]
  Part7 = Arduino Pro Mini v13
  Part3 = NRF24L01+ Breakout Board
  R4 = Resistor [tolerance=±5% resistance=22k package=THT]
  C1 = Electrolytic Capacitor [capacitance=10nF package="100 mil [THT, electrolytic]"]
  U1 = MIC [package=mic-9.7mm]

nets:
  GND: J1.pin1, Part7.GND, Part3.GND, U1.2
  N1: J1.pin2, Part7.RAW
  VCC: Part7.VCC, Part3.VCC, R4.Pin_0
  N2: Part7.A1, C1.-
  N3: Part7.D13/SCK, Part3.SCK
  N4: Part7.D12/MISO, Part3.MISO
  N5: Part7.D11_PWM/MOSI, Part3.MOSI
  N6: Part7.D8, Part3.CE
  N7: Part7.D7, Part3.CS
  N8: R4.Pin_1, C1.+, U1.1

custom parts:
  Arduino Pro Mini v13: It's blue! It's thin! It's the Arduino Pro Mini! SparkFun's minimal design approach to Arduino. This is a 5V Arduino running the 16MHz bootloader. Arduino Pro Mini does not come with connectors populated so that you can solder in any connector or wire with any orientation you need. We recommend first time Arduino users start with the Uno R3. It's a great board that will get you up and running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
