# Fritzing sketch radar (saved by Fritzing 0.9.3b)
circuit board: 6.59456cm x 5.51905cm
breadboards: 1

parts:
  Part1 = Arduino Nano (Rev3.0)
  SW-1 = Vibration sensor module
  LED1 = smd LED [color="Red (633nm)" package="0805 [SMD]"]
  Part3 = NRF24L01+ Breakout Board
  R1 = Resistor [tolerance=±5% resistance=220 package=THT]
  J1 = double row female pin header, 4 pins [form="♀ (female)"]  # not connected
  JP1 = Header 4 [package=screwterminal-3.5mm-4_lock]  # not connected
  Mic1 = KY-038  # not connected

nets:
  N1: Part1.D2, R1.Pin_0
  N2: Part1.D3, SW-1.Digital_output
  N3: Part1.D7, Part3.CS
  N4: Part1.D8, Part3.CE
  N5: Part1.D11/MOSI, Part3.MOSI
  N6: Part1.D12/MISO, Part3.MISO
  N7: Part1.D13/SCK, Part3.SCK
  N8: SW-1.Ground, LED1.cathode
  N9: LED1.anode, R1.Pin_1

custom parts:
  Vibration sensor module: Single-roller type full induction trigger switch. When no vibration or tilt, the product is ON conduction state, and in the steady state, when a vibration or tilt, the switch will be rendered instantly disconnect the conductive resistance increases, generating a current pulse signal, thereby triggering circuit. The default state of the swith is close Digital output Supply voltage:3.3V-5V On-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
  KY-038: ky-038 Microphone sound sensor module
